// Logisim project HFBI-PB_101_remade_2.circ as structural Verilog: 2 circuits, main circuit user
module user (
  input  Opcode_Command,
  input  Operand_Argument
);

  wire Execute_Command_out, hfbi_pb_100_1_l0, hfbi_pb_100_1_l1;

  Button Execute_Command (.out(Execute_Command_out));
  LED led_1 (.in(hfbi_pb_100_1_l1));
  LED led_2 (.in(hfbi_pb_100_1_l0));
  HFBI_PB_100 hfbi_pb_100_1 (
    .btn(Execute_Command_out), .C(Opcode_Command), .A(Operand_Argument), .L0(hfbi_pb_100_1_l0),
    .L1(hfbi_pb_100_1_l1));
endmodule

module HFBI_PB_100 (
  input  btn,
  input  C,
  input  A,
  output L0,
  output L1
);

  wire and_1_out, and_2_out, and_3_out, and_4_out, and_5_out, and_6_out, and_7_out, buffer_1_out,
       clock_1_out, d_ff_3_q, d_ff_4_q, Focus_2_qn, Focus_3_q, Focus_3_qn, Focus_qn, not_1_out;

  Clock clock_1 (.out(clock_1_out));
  and and_1 (and_1_out, Focus_qn, clock_1_out);
  and and_2 (and_2_out, clock_1_out, Focus_2_qn);
  not not_1 (not_1_out, C);
  and and_3 (and_3_out, btn, not_1_out, Focus_3_qn);
  and and_4 (and_4_out, btn, not_1_out, Focus_3_q);
  and and_5 (and_5_out, btn, C, Focus_3_qn);
  and and_6 (and_6_out, btn, C, Focus_3_q);
  buf buffer_1 (buffer_1_out, and_7_out);
  and and_7 (and_7_out, btn, C, A);
  D_Flip_Flop d_ff_1 (.clk(and_1_out), .D(d_ff_3_q), .Q(L0));  // open: Qn, preset, en, reset
  D_Flip_Flop d_ff_2 (.clk(and_2_out), .D(d_ff_4_q), .Q(L1));  // open: Qn, preset, en, reset
  D_Flip_Flop d_ff_3 (.clk(and_3_out), .D(A), .Q(d_ff_3_q));  // open: Qn, preset, en, reset
  D_Flip_Flop d_ff_4 (.clk(and_4_out), .D(A), .Q(d_ff_4_q));  // open: Qn, preset, en, reset
  T_Flip_Flop Focus (.clk(and_5_out), .T(and_5_out), .Qn(Focus_qn));  // open: Q, preset, reset, en
  T_Flip_Flop Focus_2 (.clk(and_6_out), .T(and_6_out), .Qn(Focus_2_qn));  // open: Q, preset, reset, en
  T_Flip_Flop Focus_3 (.clk(buffer_1_out), .Q(Focus_3_q), .Qn(Focus_3_qn));  // open: T, preset, reset, en
endmodule
